# Fritzing sketch Schematic (saved by Fritzing 0.9.3b)
breadboards: 1

parts:
  MCU1 = Raspberry Pi Zero
  XFW-002 = HX711 Weighing Sensor Module
  LM317T = Voltage Regulator [package=to220-adj]
  R1 = TRIMPOT [package=3386u]
  R2 = Resistor [tolerance=±5% resistance=68 package=THT]
  Q1 = NPN-Transistor [package="TO92 [THT]"]
  Q2 = NPN-Transistor [package="TO92 [THT]"]
  R3 = Resistor [tolerance=±5% resistance=1k package=THT]
  R4 = Resistor [tolerance=±5% resistance=1k package=THT]
  JP1 = Header 3 [package=screwterminal-3.5mm-3_lock.007s]
  Load_Cell = Header 4 [package=molex-1x4_lock]

nets:
  3.3V: MCU1.pin_1, XFW-002.VCC, LM317T.IN
  dial_reset: MCU1.pin_3, R4.Pin_1
  dial_read: MCU1.pin_5, R3.Pin_1
  GND: MCU1.pin_6, MCU1.pin_39, XFW-002.GND, R2.Pin_0, Q2.C, JP1.3
  DT: MCU1.pin_29, XFW-002.DO/RX
  SCK: MCU1.pin_31, XFW-002.CK/TX
  red: XFW-002.E+, Load_Cell.4
  black: XFW-002.E-, Load_Cell.1
  white: XFW-002.A+, Load_Cell.3
  green: XFW-002.A-, Load_Cell.2
  N1: LM317T.ADJ, R1.CCW, R2.Pin_1
  1.5V: LM317T.OUT, R1.WIPER, Q1.C
  Dial Power: Q1.E, JP1.1
  N2: Q1.B, R4.Pin_0
  Dial Switch: Q2.E, JP1.2
  N3: Q2.B, R3.Pin_0

notes:
  This header represents the load cell. It is a wheatstone bridge with colored wires corresponding to the label names
  This header represents wires broken out from the dial indicator data converter. Dial Power is red, Dial switch is blue, ground is yellow
